# Fritzing sketch breadboard (saved by Fritzing 0.9.4)
breadboards: 1

parts:
  ESP1 = ESP32-DevkitC
  Part1 = Adafruit Pixie [part_number="Adafruit #2741"]
  Part2 = Adafruit DRV8833 DC/Stepper Motor Driver [part_number="Adafruit #3297"]
  M1 = DC Motor
  J1 = Screw terminal - 2 pins [package=THT]

nets:
  N1: ESP1.IO25, Part2.AIN1
  N2: ESP1.IO26, Part2.AIN2
  N3: ESP1.IO27, Part1.IN
  GND: ESP1.GND, Part2.GND
  N4: ESP1.5V, Part2.VMOTOR, Part2.!SLEEP
  N5: Part1.5V, J1.pin1
  N6: Part1.GND, J1.pin2
  N7: Part2.AOUT2, M1.pin_1
  N8: Part2.AOUT1, M1.pin_2

custom parts:
  Adafruit Pixie: NeoPixels are plenty bright, suuuure. BUT ARE THEY 3 WATTS BRIGHT? No! They are not! That's why you need a Pixie. These chainable smart LEDs are not only super-smart, they are ridonkulously bright with 3W total, compared to 0.2W of a 'standard' NeoPixel. Designed by Ytai Ben-Tsvi, these are the ultimate in LEDs.
  Adafruit DRV8833 DC/Stepper Motor Driver: Spin two DC motors or step one bi-polar or uni-polar stepper with up to 1.2A per channel using the DRV8833. This motor driver chip is a nice alternative to the TB6612 driver. Like that chip, you get 2 full H-bridges, but this chip is better for low voltage uses (can run from 2.7V up to 10.8V motor power) and has built in current limiting capability. We set it up for 1A current limiting so you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
